// Logisim project Traffic-Light-with-logisim.circ as structural Verilog: 3 circuits, main circuit main
module main (
  input  in_1,
  output [4:0] out_2
);

  wire clock_1_out, contador_1_d0, contador_1_d1, contador_1_d2, contador_1_d3, contador_1_d4,
       logicasemaforo_1_amarelo, logicasemaforo_1_verde, logicasemaforo_1_vermelho;

  Clock clock_1 (.out(clock_1_out));
  D_Flip_Flop d_ff_1 (.clk(clock_1_out), .D(contador_1_d4), .Q(out_2[4]), .reset(in_1));  // open: Qn, preset, en
  D_Flip_Flop d_ff_2 (.clk(clock_1_out), .D(contador_1_d3), .Q(out_2[3]), .reset(in_1));  // open: Qn, preset, en
  D_Flip_Flop d_ff_3 (.clk(clock_1_out), .D(contador_1_d2), .Q(out_2[2]), .reset(in_1));  // open: Qn, preset, en
  D_Flip_Flop d_ff_4 (.clk(clock_1_out), .D(contador_1_d1), .Q(out_2[1]), .reset(in_1));  // open: Qn, preset, en
  CONTADOR contador_1 (
    .Q4(out_2[4]), .Q3(out_2[3]), .Q2(out_2[2]), .Q1(out_2[1]), .Q0(out_2[0]), .D4(contador_1_d4),
    .D3(contador_1_d3), .D2(contador_1_d2), .D1(contador_1_d1), .D0(contador_1_d0));
  LOGICASEMAFORO logicasemaforo_1 (
    .Q4(out_2[4]), .Q3(out_2[3]), .Q2(out_2[2]), .Q1(out_2[1]), .Q0(out_2[0]),
    .VERMELHO(logicasemaforo_1_vermelho), .AMARELO(logicasemaforo_1_amarelo), .VERDE(logicasemaforo_1_verde));
  D_Flip_Flop d_ff_5 (.clk(clock_1_out), .D(contador_1_d0), .Q(out_2[0]), .reset(in_1));  // open: Qn, preset, en
  LED led_1 (.in(logicasemaforo_1_vermelho));
  LED led_2 (.in(logicasemaforo_1_amarelo));
  LED led_3 (.in(logicasemaforo_1_verde));

  // Notes on the sheet:
  //   D Flip flop
  //   Delay flip flop 
  //   Data flip flop
  //   10110=green
  //   00110=red
  //   11110=yellow
  //   CONTADOR
  //   Spanish word,Electrical Counter
  //   It records the number of times an event or impulse occurs
endmodule

module CONTADOR (
  input  Q4,
  input  Q3,
  input  Q2,
  input  Q1,
  input  Q0,
  output D4,
  output D3,
  output D2,
  output D1,
  output D0
);

  wire and_1_out, and_2_out, and_3_out, and_4_out, and_5_out, and_6_out, and_7_out, and_8_out, and_9_out,
       and_10_out, and_11_out, and_12_out, and_13_out, and_14_out, not_1_out, not_2_out, not_3_out,
       not_4_out, not_5_out, not_6_out, not_7_out, not_8_out, not_9_out, not_10_out, not_11_out, not_12_out,
       not_13_out, not_14_out;

  not not_1 (not_1_out, Q4);
  not not_2 (not_2_out, Q3);
  not not_3 (not_3_out, Q2);
  not not_4 (not_4_out, Q1);
  not not_5 (not_5_out, Q0);
  not not_6 (not_6_out, Q3);
  not not_7 (not_7_out, Q2);
  not not_8 (not_8_out, Q1);
  not not_9 (not_9_out, Q0);
  not not_10 (not_10_out, Q2);
  not not_11 (not_11_out, Q1);
  not not_12 (not_12_out, Q0);
  not not_13 (not_13_out, Q1);
  not not_14 (not_14_out, Q0);
  not not_15 (D0, Q0);
  and and_1 (and_1_out, not_1_out, Q3, Q2, Q1, Q0);
  and and_2 (and_2_out, Q4, not_2_out);
  and and_3 (and_3_out, Q4, not_3_out);
  and and_4 (and_4_out, Q4, not_4_out);
  and and_5 (and_5_out, Q4, not_5_out);
  and and_6 (and_6_out, not_6_out, Q2, Q1, Q0);
  and and_7 (and_7_out, Q3, not_7_out);
  and and_8 (and_8_out, Q3, not_8_out);
  and and_9 (and_9_out, Q3, not_9_out);
  and and_10 (and_10_out, not_10_out, Q1, Q0);
  and and_11 (and_11_out, Q2, not_11_out);
  and and_12 (and_12_out, Q2, not_12_out);
  and and_13 (and_13_out, not_13_out, Q0);
  and and_14 (and_14_out, Q1, not_14_out);
  or or_1 (D4, and_1_out, and_2_out, and_3_out, and_4_out, and_5_out);
  or or_2 (D3, and_6_out, and_7_out, and_8_out, and_9_out);
  or or_3 (D2, and_10_out, and_11_out, and_12_out);
  or or_4 (D1, and_13_out, and_14_out);
endmodule

module LOGICASEMAFORO (
  input  Q4,
  input  Q3,
  input  Q2,
  input  Q1,
  input  Q0,
  output VERMELHO,
  output AMARELO,
  output VERDE
);

  wire and_2_out, and_3_out, and_4_out, and_5_out, and_6_out, and_7_out, not_1_out, not_2_out, not_3_out,
       not_4_out, not_5_out, not_6_out, not_7_out, not_8_out, not_9_out, not_10_out;

  not not_1 (not_1_out, Q3);
  not not_2 (not_2_out, Q2);
  not not_3 (not_3_out, Q3);
  not not_4 (not_4_out, Q1);
  not not_5 (not_5_out, Q0);
  and and_1 (AMARELO, Q4, Q3, Q2, Q1);
  not not_6 (not_6_out, Q3);
  not not_7 (not_7_out, Q3);
  not not_8 (not_8_out, Q2);
  not not_9 (not_9_out, Q1);
  not not_10 (not_10_out, Q4);
  and and_2 (and_2_out, not_1_out, not_2_out);
  and and_3 (and_3_out, not_3_out, not_4_out, not_5_out);
  and and_4 (and_4_out, Q4, not_6_out, Q2, Q0);
  and and_5 (and_5_out, Q4, not_7_out, Q2, Q1);
  and and_6 (and_6_out, Q4, Q3, not_8_out);
  and and_7 (and_7_out, Q4, Q3, not_9_out);
  or or_1 (VERMELHO, not_10_out, and_2_out, and_3_out);
  or or_2 (VERDE, and_4_out, and_5_out, and_6_out, and_7_out);
endmodule
